# Fritzing sketch exDotMatrixS_Circuit (saved by Fritzing 0.9.3b)
breadboards: 1

parts:
  Disp1 = LBT2088AH [part_number=LBT2088AH]
  부품1 = Arduino Due (Rev2b)
  R1 = Resistor [tolerance=±5% resistance=220 package=THT]
  R2 = Resistor [tolerance=±5% resistance=220 package=THT]
  R3 = Resistor [tolerance=±5% resistance=220 package=THT]
  R4 = Resistor [tolerance=±5% resistance=220 package=THT]
  R5 = Resistor [tolerance=±5% resistance=220 package=THT]
  R6 = Resistor [tolerance=±5% resistance=220 package=THT]
  R7 = Resistor [tolerance=±5% resistance=220 package=THT]
  R8 = Resistor [tolerance=±5% resistance=220 package=THT]

nets:
  N1: Disp1.pin1, R2.Pin_0
  N2: Disp1.pin2, R3.Pin_0
  N3: Disp1.pin_3, 부품1.D27
  N4: Disp1.pin_4, 부품1.D29
  N5: Disp1.pin_5, R4.Pin_0
  N6: Disp1.pin_6, 부품1.D33
  N7: Disp1.pin_7, R5.Pin_0
  N8: Disp1.pin_8, R1.Pin_0
  N9: Disp1.pin_9, R6.Pin_1
  N10: Disp1.pin_10, 부품1.D41
  N11: Disp1.pin_11, 부품1.D43
  N12: Disp1.pin_12, 부품1.D45
  N13: Disp1.pin_13, 부품1.D47
  N14: Disp1.pin_14, R7.Pin_1
  N15: Disp1.pin_15, 부품1.D51
  N16: Disp1.pin_16, R8.Pin_1
  N17: 부품1.D23, R2.Pin_1
  N18: 부품1.D25, R3.Pin_1
  N19: 부품1.D31, R4.Pin_1
  N20: 부품1.D35, R5.Pin_1
  N21: 부품1.D37, R1.Pin_1
  N22: 부품1.D39, R6.Pin_0
  N23: 부품1.D49, R7.Pin_0
  N24: 부품1.D53, R8.Pin_0
