# Fritzing sketch exDotMatrixS_SR_Circuit (saved by Fritzing 0.9.3b)
breadboards: 2

parts:
  Disp1 = LBT2088AH [part_number=LBT2088AH]
  부품1 = Arduino Due (Rev2b)
  R1 = Resistor [tolerance=±5% resistance=220 package=THT]
  R2 = Resistor [tolerance=±5% resistance=220 package=THT]
  R3 = Resistor [tolerance=±5% resistance=220 package=THT]
  R4 = Resistor [tolerance=±5% resistance=220 package=THT]
  R5 = Resistor [tolerance=±5% resistance=220 package=THT]
  R6 = Resistor [tolerance=±5% resistance=220 package=THT]
  R7 = Resistor [tolerance=±5% resistance=220 package=THT]
  R8 = Resistor [tolerance=±5% resistance=220 package=THT]
  U1 = 74HC595 [package="DIP16 [THT]"]
  U2 = 74HC595 [package="DIP16 [THT]"]

nets:
  N1: Disp1.pin1, R1.Pin_1
  N2: Disp1.pin2, R7.Pin_1
  N3: Disp1.pin_3, U2.Q1
  N4: Disp1.pin_4, U2.Q2
  N5: Disp1.pin_5, R8.Pin_1
  N6: Disp1.pin_6, U2.Q4
  N7: Disp1.pin_7, R6.Pin_1
  N8: Disp1.pin_8, R4.Pin_1
  N9: Disp1.pin_9, R2.Pin_0
  N10: Disp1.pin_10, U2.Q3
  N11: Disp1.pin_11, U2.Q5
  N12: Disp1.pin_12, R5.Pin_0
  N13: Disp1.pin_13, U2.Q0
  N14: Disp1.pin_14, R3.Pin_0
  N15: Disp1.pin_15, U2.Q6
  N16: Disp1.pin_16, U2.Q7
  VCC: 부품1.5V, U1.MR, U1.VCC, U2.MR, U2.VCC
  N17: 부품1.GND, U1.OE, U2.OE
  N18: 부품1.D44, U2.DS
  N19: 부품1.D46, U1.ST_CP, U2.ST_CP
  N20: 부품1.D48, U1.SH_CP, U2.SH_CP
  N21: R1.Pin_0, U1.Q4
  N22: R2.Pin_1, U1.Q0
  N23: R3.Pin_1, U1.Q1
  N24: R4.Pin_0, U1.Q2
  N25: R5.Pin_1, U1.Q3
  N26: R6.Pin_0, U1.Q5
  N27: R7.Pin_0, U1.Q6
  N28: R8.Pin_0, U1.Q7
  N29: U1.DS, U2.Q7'
