# Fritzing sketch exDutyMotorPos_Circuit (saved by Fritzing 0.9.3b)
breadboards: 1

parts:
  부품1 = Arduino Due (Rev2b)
  S1 = H-Bridge with L298N
  M1 = DC Motor
  U1 = ENCODER-QUADRATURE [package=encoder-16mm-quad]
  Q1 = PHOTOTRANSISTOR REFLECTIVE OBJECT SENSOR [package=qrb1114-side]
  Q2 = PHOTOTRANSISTOR REFLECTIVE OBJECT SENSOR [package=qrb1114-side]
  Q3 = PHOTOTRANSISTOR REFLECTIVE OBJECT SENSOR [package=qrb1114-side]
  R1 = Resistor [tolerance=±5% resistance=100 package=THT]
  R2 = Resistor [tolerance=±5% resistance=6.6k package=THT]
  R3 = Resistor [tolerance=±5% resistance=100 package=THT]
  R4 = Resistor [tolerance=±5% resistance=6.6k package=THT]
  R5 = Resistor [tolerance=±5% resistance=100 package=THT]
  R6 = Resistor [tolerance=±5% resistance=6.6k package=THT]

nets:
  N1: 부품1.IOREF, R1.Pin_0, R2.Pin_0, R3.Pin_0, R4.Pin_0, R5.Pin_0, R6.Pin_0
  5V: 부품1.5V, S1.5V, U1.B
  GND: 부품1.GND, S1.GND, U1.C, Q1.E, Q1.K, Q2.E, Q2.K, Q3.E, Q3.K
  N2: 부품1.D2_PWM, S1.ENA
  N3: 부품1.D30, S1.IN1
  N4: 부품1.D32, S1.IN2
  N5: 부품1.D34, U1.A
  N6: 부품1.D37, Q1.C, R2.Pin_1
  N7: 부품1.D39, Q2.C, R4.Pin_1
  N8: 부품1.D41, Q3.C, R6.Pin_1
  N9: S1.M1-01, M1.pin_2
  N10: S1.M1-02, M1.pin_1
  N11: S1.M2-01, S1.M2-02, S1.ENA-5V
  N12: Q1.A, R1.Pin_1
  N13: Q2.A, R3.Pin_1
  N14: Q3.A, R5.Pin_1

custom parts:
  H-Bridge with L298N: h-bridge
