# Fritzing sketch exFnd1S_SR_Circuit (saved by Fritzing 0.9.3b)
breadboards: 1

parts:
  부품1 = Arduino Due (Rev2b)
  7_Segment1 = 7 Segment Display
  U1 = 74HC595 [package="DIP16 [THT]"]
  R1 = Resistor [tolerance=±5% resistance=220 package=THT]
  R2 = Resistor [tolerance=±5% resistance=220 package=THT]
  R3 = Resistor [tolerance=±5% resistance=220 package=THT]
  R4 = Resistor [tolerance=±5% resistance=220 package=THT]
  R5 = Resistor [tolerance=±5% resistance=220 package=THT]
  R6 = Resistor [tolerance=±5% resistance=220 package=THT]
  R7 = Resistor [tolerance=±5% resistance=220 package=THT]
  R8 = Resistor [tolerance=±5% resistance=220 package=THT]

nets:
  5V: 부품1.5V, U1.MR, U1.VCC
  GND: 부품1.GND, 7_Segment1.common_cathode, U1.GND, U1.OE
  N1: 부품1.D22, U1.SH_CP
  N2: 부품1.D24, U1.ST_CP
  N3: 부품1.D26, U1.DS
  N4: 7_Segment1.Segment_E, R5.Pin_1
  N5: 7_Segment1.Segment_D, R6.Pin_1
  N6: 7_Segment1.Segment_C, R7.Pin_1
  N7: 7_Segment1.Segment_DP, R2.Pin_1
  N8: 7_Segment1.Segment_B, R8.Pin_1
  N9: 7_Segment1.Segment_A, R1.Pin_1
  N10: 7_Segment1.Segment_F, R4.Pin_1
  N11: 7_Segment1.Segment_G, R3.Pin_1
  N12: U1.Q1, R8.Pin_0
  N13: U1.Q2, R7.Pin_0
  N14: U1.Q3, R6.Pin_0
  N15: U1.Q4, R5.Pin_0
  N16: U1.Q5, R4.Pin_0
  N17: U1.Q6, R3.Pin_0
  N18: U1.Q7, R2.Pin_0
  N19: U1.Q0, R1.Pin_0
