# Fritzing sketch exFnd4S_Circuit (saved by Fritzing 0.9.3b)
breadboards: 1

parts:
  부품1 = Arduino Due (Rev2b)
  R1 = Resistor [tolerance=±5% resistance=220 package=THT]
  R2 = Resistor [tolerance=±5% resistance=220 package=THT]
  R3 = Resistor [tolerance=±5% resistance=220 package=THT]
  R4 = Resistor [tolerance=±5% resistance=220 package=THT]
  R5 = Resistor [tolerance=±5% resistance=220 package=THT]
  R8 = Resistor [tolerance=±5% resistance=220 package=THT]
  R9 = Resistor [tolerance=±5% resistance=220 package=THT]
  R12 = Resistor [tolerance=±5% resistance=220 package=THT]
  U1 = 7-SEGMENT-4DIGIT [package=7-segment-4digit-5641]

nets:
  N1: 부품1.D29, U1.DIG4
  N2: 부품1.D31, R5.Pin_1
  N3: 부품1.D33, R4.Pin_1
  N4: 부품1.D35, R12.Pin_1
  N5: 부품1.D37, U1.DIG3
  N6: 부품1.D39, U1.DIG2
  N7: 부품1.D41, R9.Pin_0
  N8: 부품1.D43, R8.Pin_0
  N9: 부품1.D45, U1.DIG1
  N10: 부품1.D47, R1.Pin_0
  N11: 부품1.D49, R2.Pin_0
  N12: 부품1.D51, R3.Pin_0
  N13: R1.Pin_1, U1.DP
  N14: R2.Pin_1, U1.D
  N15: R3.Pin_1, U1.E
  N16: R4.Pin_0, U1.C
  N17: R5.Pin_0, U1.G
  N18: R8.Pin_1, U1.A
  N19: R12.Pin_0, U1.B

custom parts:
  7-SEGMENT-4DIGIT: if you need make parts, send me e-mail and write. Price 1 part=0.9 WMZ (http://www.wmtransfer.com/) ~ 0.9 Euro
