# Fritzing sketch exFnd4S_SR2_Circuit (saved by Fritzing 0.9.3b)
breadboards: 2

parts:
  U1 = 7-SEGMENT-4DIGIT [package=7-segment-4digit-5641]
  U2 = 74HC595 [package="DIP16 [THT]"]
  R1 = Resistor [tolerance=±5% resistance=220 package=THT]
  R2 = Resistor [tolerance=±5% resistance=220 package=THT]
  R3 = Resistor [tolerance=±5% resistance=220 package=THT]
  R4 = Resistor [tolerance=±5% resistance=220 package=THT]
  R5 = Resistor [tolerance=±5% resistance=220 package=THT]
  R6 = Resistor [tolerance=±5% resistance=220 package=THT]
  R7 = Resistor [tolerance=±5% resistance=220 package=THT]
  R8 = Resistor [tolerance=±5% resistance=220 package=THT]
  부품1 = Arduino Due (Rev2b)
  U3 = 74HC595 [package="DIP16 [THT]"]

nets:
  N1: U1.DIG2, U3.Q1
  N2: U1.DIG3, U3.Q2
  N3: U1.DIG4, U3.Q3
  N4: U1.A, R1.Pin_0
  N5: U1.B, R2.Pin_0
  N6: U1.C, R3.Pin_0
  N7: U1.D, R4.Pin_0
  N8: U1.E, R5.Pin_0
  N9: U1.F, R6.Pin_0
  N10: U1.G, R7.Pin_0
  N11: U1.DP, R8.Pin_0
  N12: U1.DIG1, U3.Q0
  N13: U2.Q1, R2.Pin_1
  N14: U2.Q2, R3.Pin_1
  N15: U2.Q3, R4.Pin_1
  N16: U2.Q4, R5.Pin_1
  N17: U2.Q5, R6.Pin_1
  N18: U2.Q6, R7.Pin_1
  N19: U2.Q7, R8.Pin_1
  GND: U2.GND, U2.OE, 부품1.GND, U3.GND
  N20: U2.Q7', U3.DS
  VCC: U2.MR, U2.VCC, 부품1.5V
  N21: U2.SH_CP, 부품1.D40, U3.SH_CP
  N22: U2.ST_CP, 부품1.D42, U3.ST_CP
  N23: U2.DS, 부품1.D46
  N24: U2.Q0, R1.Pin_1
  N25: U3.MR, U3.VCC

custom parts:
  7-SEGMENT-4DIGIT: if you need make parts, send me e-mail and write. Price 1 part=0.9 WMZ (http://www.wmtransfer.com/) ~ 0.9 Euro
