# Fritzing sketch exFnd4Sx2_SR_Circuit (saved by Fritzing 0.9.3b)
breadboards: 2

parts:
  U1 = 7-SEGMENT-4DIGIT [package=7-segment-4digit-5641]
  U2 = 74HC595 [package="DIP16 [THT]"]
  R1 = Resistor [tolerance=±5% resistance=220 package=THT]
  R2 = Resistor [tolerance=±5% resistance=220 package=THT]
  R3 = Resistor [tolerance=±5% resistance=220 package=THT]
  R4 = Resistor [tolerance=±5% resistance=220 package=THT]
  R5 = Resistor [tolerance=±5% resistance=220 package=THT]
  R6 = Resistor [tolerance=±5% resistance=220 package=THT]
  R7 = Resistor [tolerance=±5% resistance=220 package=THT]
  R8 = Resistor [tolerance=±5% resistance=220 package=THT]
  부품1 = Arduino Due (Rev2b)
  U3 = 7-SEGMENT-4DIGIT [package=7-segment-4digit-5641]
  U4 = 74HC595 [package="DIP16 [THT]"]
  R9 = Resistor [tolerance=±5% resistance=220 package=THT]
  R10 = Resistor [tolerance=±5% resistance=220 package=THT]
  R11 = Resistor [tolerance=±5% resistance=220 package=THT]
  R12 = Resistor [tolerance=±5% resistance=220 package=THT]
  R13 = Resistor [tolerance=±5% resistance=220 package=THT]
  R14 = Resistor [tolerance=±5% resistance=220 package=THT]
  R15 = Resistor [tolerance=±5% resistance=220 package=THT]
  R16 = Resistor [tolerance=±5% resistance=220 package=THT]

nets:
  N1: U1.DIG2, 부품1.D45
  N2: U1.DIG3, 부품1.D43
  N3: U1.DIG4, 부품1.D41
  N4: U1.A, R1.Pin_0
  N5: U1.B, R2.Pin_0
  N6: U1.C, R3.Pin_0
  N7: U1.D, R4.Pin_0
  N8: U1.E, R5.Pin_0
  N9: U1.F, R6.Pin_0
  N10: U1.G, R7.Pin_0
  N11: U1.DP, R8.Pin_0
  N12: U1.DIG1, 부품1.D47
  N13: U2.Q1, R2.Pin_1
  N14: U2.Q2, R3.Pin_1
  N15: U2.Q3, R4.Pin_1
  N16: U2.Q4, R5.Pin_1
  N17: U2.Q5, R6.Pin_1
  N18: U2.Q6, R7.Pin_1
  N19: U2.Q7, R8.Pin_1
  GND: U2.GND, U2.OE, 부품1.GND, U4.GND, U4.OE
  VCC: U2.MR, U2.VCC, 부품1.5V, U4.MR, U4.VCC
  N20: U2.SH_CP, 부품1.D49
  N21: U2.ST_CP, 부품1.D51
  N22: U2.DS, 부품1.D53
  N23: U2.Q0, R1.Pin_1
  N24: 부품1.D27, U3.DIG4
  N25: 부품1.D29, U3.DIG3
  N26: 부품1.D31, U3.DIG2
  N27: 부품1.D33, U3.DIG1
  N28: 부품1.D35, U4.SH_CP
  N29: 부품1.D37, U4.ST_CP
  N30: 부품1.D39, U4.DS
  N31: U3.A, R16.Pin_0
  N32: U3.B, R15.Pin_0
  N33: U3.C, R14.Pin_0
  N34: U3.D, R13.Pin_0
  N35: U3.E, R12.Pin_0
  N36: U3.F, R11.Pin_0
  N37: U3.G, R10.Pin_0
  N38: U3.DP, R9.Pin_0
  N39: U4.Q1, R15.Pin_1
  N40: U4.Q2, R14.Pin_1
  N41: U4.Q3, R13.Pin_1
  N42: U4.Q4, R12.Pin_1
  N43: U4.Q5, R11.Pin_1
  N44: U4.Q6, R10.Pin_1
  N45: U4.Q7, R9.Pin_1
  N46: U4.Q0, R16.Pin_1

custom parts:
  7-SEGMENT-4DIGIT: if you need make parts, send me e-mail and write. Price 1 part=0.9 WMZ (http://www.wmtransfer.com/) ~ 0.9 Euro
