# Fritzing sketch exSensor_Circuit (saved by Fritzing 0.9.3b)
breadboards: 1

parts:
  부품1 = Arduino Due (Rev2b)
  R1 = PHOTOCELL [package=photocell-kit]
  R2 = Resistor [tolerance=±5% resistance=10k package=THT]

nets:
  N1: 부품1.A8, R1.P$2, R2.Pin_0
  N2: 부품1.5V, R2.Pin_1
  N3: 부품1.GND, R1.P$1
