# Fritzing sketch exSolenoid2P_Circuit (saved by Fritzing 0.9.3b)
breadboards: 1

parts:
  S1 = H-Bridge with L298N
  부품1 = Arduino Due (Rev2b)
  L1 = Solenoid
  VCC1 = Battery block 9V

nets:
  N1: S1.12V, VCC1.+
  GND: S1.GND, 부품1.GND, VCC1.-
  5V: S1.5V, 부품1.5V
  N2: S1.IN3, 부품1.D44
  N3: S1.IN4, 부품1.D46
  N4: S1.ENB, 부품1.D2_PWM
  N5: S1.M2-01, L1.pin2
  N6: S1.M2-02, L1.pin1

custom parts:
  H-Bridge with L298N: h-bridge
