# Fritzing sketch exSwitch_Circuit (saved by Fritzing 0.9.3b)
breadboards: 1

parts:
  부품1 = Arduino Due (Rev2b)
  S1 = Pushbutton [package="[THT]"]
  S2 = Tilt Switch [package=THT]
  LED1 = LED - 5mm [color="Yellow (595nm)" package="5 mm [THT]"]
  LED2 = LED - 5mm [color="Red (633nm)" package="5 mm [THT]"]
  R1 = Resistor [tolerance=±5% resistance=220 package=THT]
  R2 = Resistor [tolerance=±5% resistance=220 package=THT]

nets:
  N1: 부품1.D23, R2.Pin_0
  N2: 부품1.D25, R1.Pin_0
  N3: 부품1.D29, S1.Pin_3, S1.Pin_4
  N4: 부품1.D31, S2.Pin_1
  N5: 부품1.GND, S1.Pin_1, S1.Pin_2, S2.Pin_2, LED1.cathode, LED2.cathode
  N6: LED1.anode, R1.Pin_1
  N7: LED2.anode, R2.Pin_1
