# Fritzing sketch exTask2_Circuit (saved by Fritzing 0.9.3b)
circuit board: 16.2916cm x 6.84285cm
breadboards: 1

parts:
  부품1 = Arduino Due (Rev2b)
  LED1 = LED - 3mm [color="Red (633nm)" package="3 mm [THT]"]
  LED2 = LED - 3mm [color="Yellow (595nm)" package="3 mm [THT]"]
  LED3 = LED - 3mm [color="Green (570nm)" package="3 mm [THT]"]
  R1 = Resistor [tolerance=±5% resistance=330 package=THT]
  R2 = Resistor [tolerance=±5% resistance=330 package=THT]
  R3 = Resistor [tolerance=±5% resistance=330 package=THT]

nets:
  N1: 부품1.GND, LED1.cathode, LED2.cathode, LED3.cathode
  N2: 부품1.D23, R1.Pin_1
  N3: 부품1.D25, R2.Pin_1
  N4: 부품1.D27, R3.Pin_1
  N5: LED1.anode, R1.Pin_0
  N6: LED2.anode, R2.Pin_0
  N7: LED3.anode, R3.Pin_0
