# Fritzing sketch exDotMatrixS_SR_Circuit (saved by Fritzing 0.9.3b)
breadboards: 2

parts:
  Disp1 = LBT2088AH [part_number=LBT2088AH]
  R1 = Resistor [tolerance=±5% resistance=220 package=THT]
  R2 = Resistor [tolerance=±5% resistance=220 package=THT]
  R3 = Resistor [tolerance=±5% resistance=220 package=THT]
  R4 = Resistor [tolerance=±5% resistance=220 package=THT]
  R5 = Resistor [tolerance=±5% resistance=220 package=THT]
  R6 = Resistor [tolerance=±5% resistance=220 package=THT]
  R7 = Resistor [tolerance=±5% resistance=220 package=THT]
  R8 = Resistor [tolerance=±5% resistance=220 package=THT]
  U1 = 74HC595 [package="DIP16 [THT]"]
  U2 = 74HC595 [package="DIP16 [THT]"]
  부품2 = Arduino Nano (Rev3.0)

nets:
  N1: Disp1.pin1, R1.Pin_1
  N2: Disp1.pin2, R7.Pin_1
  N3: Disp1.pin_3, U2.Q1
  N4: Disp1.pin_4, U2.Q2
  N5: Disp1.pin_5, R8.Pin_1
  N6: Disp1.pin_6, U2.Q4
  N7: Disp1.pin_7, R6.Pin_1
  N8: Disp1.pin_8, R4.Pin_1
  N9: Disp1.pin_9, R2.Pin_0
  N10: Disp1.pin_10, U2.Q3
  N11: Disp1.pin_11, U2.Q5
  N12: Disp1.pin_12, R5.Pin_0
  N13: Disp1.pin_13, U2.Q0
  N14: Disp1.pin_14, R3.Pin_0
  N15: Disp1.pin_15, U2.Q6
  N16: Disp1.pin_16, U2.Q7
  N17: R1.Pin_0, U1.Q4
  N18: R2.Pin_1, U1.Q0
  N19: R3.Pin_1, U1.Q1
  N20: R4.Pin_0, U1.Q2
  N21: R5.Pin_1, U1.Q3
  N22: R6.Pin_0, U1.Q5
  N23: R7.Pin_0, U1.Q6
  N24: R8.Pin_0, U1.Q7
  VCC: U1.MR, U1.VCC, U2.MR, U2.VCC, 부품2.5V
  N25: U1.SH_CP, U2.SH_CP, 부품2.D5
  N26: U1.ST_CP, U2.ST_CP, 부품2.D6
  N27: U1.OE, U2.OE, 부품2.GND
  N28: U1.DS, U2.Q7'
  N29: U2.DS, 부품2.D7
