# Fritzing sketch exFnd1S_Circuit (saved by Fritzing 0.9.3b)
breadboards: 1

parts:
  부품1 = Arduino Nano (Rev3.0)
  7_Segment1 = 7 Segment Display
  R1 = Resistor [tolerance=±5% resistance=220 package=THT]
  R2 = Resistor [tolerance=±5% resistance=220 package=THT]
  R3 = Resistor [tolerance=±5% resistance=220 package=THT]
  R4 = Resistor [tolerance=±5% resistance=220 package=THT]
  R5 = Resistor [tolerance=±5% resistance=220 package=THT]
  R6 = Resistor [tolerance=±5% resistance=220 package=THT]
  R7 = Resistor [tolerance=±5% resistance=220 package=THT]
  R8 = Resistor [tolerance=±5% resistance=220 package=THT]

nets:
  N1: 부품1.GND, 7_Segment1.common_cathode
  N2: 부품1.D2, R2.Pin_1
  N3: 부품1.D3, R1.Pin_1
  N4: 부품1.D4, R3.Pin_1
  N5: 부품1.D5, R4.Pin_1
  N6: 부품1.D6, R5.Pin_0
  N7: 부품1.D7, R6.Pin_0
  N8: 부품1.D8, R7.Pin_0
  N9: 부품1.D9, R8.Pin_0
  N10: 7_Segment1.Segment_E, R6.Pin_1
  N11: 7_Segment1.Segment_D, R5.Pin_1
  N12: 7_Segment1.Segment_C, R4.Pin_0
  N13: 7_Segment1.Segment_DP, R3.Pin_0
  N14: 7_Segment1.Segment_B, R2.Pin_0
  N15: 7_Segment1.Segment_A, R1.Pin_0
  N16: 7_Segment1.Segment_F, R7.Pin_1
  N17: 7_Segment1.Segment_G, R8.Pin_1
