# Fritzing sketch exFnd1S_SR_Circuit (saved by Fritzing 0.9.3b)
breadboards: 1

parts:
  부품1 = Arduino Nano (Rev3.0)
  7_Segment1 = 7 Segment Display
  R1 = Resistor [tolerance=±5% resistance=220 package=THT]
  R2 = Resistor [tolerance=±5% resistance=220 package=THT]
  R3 = Resistor [tolerance=±5% resistance=220 package=THT]
  R4 = Resistor [tolerance=±5% resistance=220 package=THT]
  R5 = Resistor [tolerance=±5% resistance=220 package=THT]
  R6 = Resistor [tolerance=±5% resistance=220 package=THT]
  R7 = Resistor [tolerance=±5% resistance=220 package=THT]
  R8 = Resistor [tolerance=±5% resistance=220 package=THT]
  U1 = 74HC595 [package="DIP16 [THT]"]

nets:
  N1: 부품1.D2, U1.DS
  N2: 부품1.D3, U1.ST_CP
  N3: 부품1.D4, U1.SH_CP
  GND: 부품1.GND, 7_Segment1.common_cathode, U1.GND, U1.OE
  5V: 부품1.5V, U1.MR, U1.VCC
  N4: 7_Segment1.Segment_E, R5.Pin_1
  N5: 7_Segment1.Segment_D, R4.Pin_1
  N6: 7_Segment1.Segment_C, R3.Pin_1
  N7: 7_Segment1.Segment_DP, R8.Pin_1
  N8: 7_Segment1.Segment_A, R1.Pin_1
  N9: 7_Segment1.Segment_F, R6.Pin_1
  N10: 7_Segment1.Segment_G, R7.Pin_1
  N11: R1.Pin_0, U1.Q0
  N12: R2.Pin_0, U1.Q1
  N13: R3.Pin_0, U1.Q2
  N14: R4.Pin_0, U1.Q3
  N15: R5.Pin_0, U1.Q4
  N16: R6.Pin_0, U1.Q5
  N17: R7.Pin_0, U1.Q6
  N18: R8.Pin_0, U1.Q7
