# Fritzing sketch exFnd4S_Circuit (saved by Fritzing 0.9.3b)
breadboards: 3

parts:
  R13 = Resistor [tolerance=±5% resistance=220 package=THT]
  R14 = Resistor [tolerance=±5% resistance=220 package=THT]
  R15 = Resistor [tolerance=±5% resistance=220 package=THT]
  R16 = Resistor [tolerance=±5% resistance=220 package=THT]
  R17 = Resistor [tolerance=±5% resistance=220 package=THT]
  R18 = Resistor [tolerance=±5% resistance=220 package=THT]
  R19 = Resistor [tolerance=±5% resistance=220 package=THT]
  R20 = Resistor [tolerance=±5% resistance=220 package=THT]
  U2 = 7-SEGMENT-4DIGIT [package=7-segment-4digit-5641]
  부품1 = Arduino Nano (Rev3.0)

nets:
  N1: R13.Pin_0, 부품1.D4
  N2: R13.Pin_1, U2.DP
  N3: R14.Pin_0, 부품1.D3
  N4: R14.Pin_1, U2.D
  N5: R15.Pin_0, 부품1.D2
  N6: R15.Pin_1, U2.E
  N7: R16.Pin_0, U2.C
  N8: R16.Pin_1, 부품1.D11/MOSI
  N9: R17.Pin_0, U2.G
  N10: R17.Pin_1, 부품1.D12/MISO
  N11: R18.Pin_0, 부품1.D6
  N12: R18.Pin_1, U2.A
  N13: R19.Pin_0, 부품1.D7
  N14: R20.Pin_0, U2.B
  N15: R20.Pin_1, 부품1.D10
  N16: U2.DIG2, 부품1.D8
  N17: U2.DIG3, 부품1.D9
  N18: U2.DIG4, 부품1.D13/SCK
  N19: U2.DIG1, 부품1.D5

custom parts:
  7-SEGMENT-4DIGIT: if you need make parts, send me e-mail and write. Price 1 part=0.9 WMZ (http://www.wmtransfer.com/) ~ 0.9 Euro
