# Fritzing sketch exSensor_Circuit (saved by Fritzing 0.9.3b)
breadboards: 1

parts:
  R1 = Resistor [tolerance=±5% resistance=220 package=THT]
  R2 = PHOTOCELL [package=photocell-kit]
  부품1 = Arduino Nano (Rev3.0)

nets:
  N1: R1.Pin_0, R2.P$2, 부품1.A1
  N2: R1.Pin_1, 부품1.5V
  N3: R2.P$1, 부품1.GND
