# Fritzing sketch circuit (saved by Fritzing 0.9.3b)
breadboards: 1

parts:
  KY-1 = Keyes Relay [package=THT]
  부품1 = Arduino Nano (Rev3.0)

nets:
  N1: KY-1.signal, 부품1.D5
  N2: KY-1.power, 부품1.5V
  N3: KY-1.ground, 부품1.GND

custom parts:
  Keyes Relay: The Keyes 5V relay module is suitable for SCM development, home appliance control. It uses a 5V~12V TIL control signal which can control DC / AC signal.
