# Fritzing sketch exSwitch_Circuit (saved by Fritzing 0.9.3b)
breadboards: 1

parts:
  부품1 = Arduino Nano (Rev3.0)
  LED1 = LED - 5mm [color="Red (633nm)" package="5 mm [THT]"]
  LED2 = LED - 5mm [color="Yellow (595nm)" package="5 mm [THT]"]
  R1 = Resistor [tolerance=±5% resistance=220 package=THT]
  R2 = Resistor [tolerance=±5% resistance=220 package=THT]
  S1 = Pushbutton [package="[THT]"]
  S2 = Tilt Switch [package=THT]

nets:
  N1: 부품1.GND, LED1.cathode, LED2.cathode, S1.Pin_3, S1.Pin_4, S2.Pin_1
  N2: 부품1.D2, R1.Pin_1
  N3: 부품1.D3, R2.Pin_1
  N4: 부품1.D4, S1.Pin_1, S1.Pin_2
  N5: 부품1.D5, S2.Pin_2
  N6: LED1.anode, R1.Pin_0
  N7: LED2.anode, R2.Pin_0
